# Fritzing sketch Arduino WS2812B Bluetooth (saved by Fritzing 0.9.3b)

parts:
  NEOPIXEL1 = Neopixel Strip -- Black (30/m)
  Part1 = Arduino Uno (Rev3)
  JACK1 = 2.1mm Barrel Jack with Terminal Block
  Part2 = Bluetooth HC-05 Macho

nets:
  GND: NEOPIXEL1.GND, Part1.GND, JACK1.NEG
  N1: NEOPIXEL1.Din, Part1.D2
  +5V: NEOPIXEL1.+5V, Part1.VIN, JACK1.POS, Part2.VCC
  N2: Part1.D10_PWM/SS, Part2.TXD
  N3: Part1.D11_PWM/MOSI, Part2.RXD

custom parts:
  Neopixel Strip -- Black (30/m): These NeoPixel strips have 30 digitally-addressable pixel LEDs per meter and are very affordable and are only 12.5 mm wide, 10 mm if you remove the strip from the casing.
